// Logisim project digital-lock.circ as structural Verilog: 1 circuit, main circuit main
module main (
  input  My_input,
  input  Combination
);

  wire comparator_1_eq, comparator_1_gt, comparator_1_lt, or_1_out;

  Comparator #(.width(1)) comparator_1 (
    .a(Combination), .b(My_input), .gt(comparator_1_gt), .eq(comparator_1_eq), .lt(comparator_1_lt));
  LED led_1 (.in(comparator_1_eq));
  LED led_2 (.in(or_1_out));
  or or_1 (or_1_out, comparator_1_gt, comparator_1_lt);

  // Notes on the sheet:
  //   "Working" Implemenation of a 1-bit Digital Lock
  //   Correct
  //   Incorrect
endmodule
